# Fritzing sketch Badge of Awesome Fritzing (saved by Fritzing 1.0.2b)

parts:
  WeMos_D1_Mini1 = WeMos D1 Mini
  Part1 = NeoPixel NeoMatrix 8x8 [part_number=1487]

nets:
  5V: WeMos_D1_Mini1.5V, Part1.VDD
  N1: WeMos_D1_Mini1.D8, Part1.IN
  N2: WeMos_D1_Mini1.G, Part1.GND

custom parts:
  NeoPixel NeoMatrix 8x8: Put on your sunglasses before wiring up this LED matrix - 64 eye-blistering RGB LEDs adorn the NeoMatrix for a blast of configurable color. Arranged in an 8x8 matrix, each pixel is individually addressable. Only one microcontroller pin is required to control all the LEDs, and you get 24 bit color for each LED.
